// Logisim project Project1Given.circ as structural Verilog: 4 circuits, main circuit main
module main (
  input  in_1,
  input  in_2,
  input  in_3,
  input  in_4,
  input  Five,
  output N,
  output E,
  output [3:0] out_8
);

  wire fiveseven_1_a, fiveseven_1_b, fiveseven_1_c, fiveseven_1_d, fiveseven_1_e, fiveseven_1_f,
       fiveseven_1_g;

  Compare compare_1 (.X0(1'b1), .X1(1'b0), .X2(1'b1), .Y0(1'b1), .Y1(1'b1), .Y2(1'b1), .N(N), .E(E));
  Gray gray_1 (.B0(1'b1), .B1(1'b0), .B2(1'b1), .B3(1'b1), .G0(out_8[0]), .G1(out_8[1]), .G2(out_8[2]), .G3(out_8[3]));
  FiveSeven fiveseven_1 (
    .V(in_1), .W(in_2), .X(in_3), .Y(in_4), .Z(Five), .A(fiveseven_1_a), .B(fiveseven_1_b),
    .C(fiveseven_1_c), .D(fiveseven_1_d), .E(fiveseven_1_e), .F(fiveseven_1_f), .G(fiveseven_1_g));
  _7_Segment_Display u_7_segment_display_1 (
    .g(fiveseven_1_g), .f(fiveseven_1_f), .a(fiveseven_1_a), .b(fiveseven_1_b), .e(fiveseven_1_e),
    .d(fiveseven_1_d), .c(fiveseven_1_c));  // open: dp
endmodule

module Compare (
  input  X0,
  input  X1,
  input  X2,
  input  Y0,
  input  Y1,
  input  Y2,
  output N,
  output E
);

  wire and_1_out, and_2_out, and_3_out, and_4_out, and_5_out, and_6_out, and_10_out, and_11_out, NOTX0,
       NOTX0_Y0, NOTX1, NOTX1_Y1, NOTX2, NOTX2_Y2, NOTY0, NOTY1, NOTY2, XNOR_X0Y0, XNOR_X1Y1, XNOR_X2Y2;

  not not_1 (NOTX0, X0);
  not not_2 (NOTX1, X1);
  not not_3 (NOTX2, X2);
  not not_4 (NOTY0, Y0);
  not not_5 (NOTY1, Y1);
  not not_6 (NOTY2, Y2);
  and and_1 (and_1_out, X0, Y0);
  and and_2 (and_2_out, X1, Y1);
  and and_3 (and_3_out, X2, Y2);
  and and_4 (and_4_out, NOTX0, NOTY0);
  and and_5 (and_5_out, NOTX1, NOTY1);
  and and_6 (and_6_out, NOTX2, NOTY2);
  or or_1 (XNOR_X0Y0, and_1_out, and_4_out);
  or or_2 (XNOR_X1Y1, and_2_out, and_5_out);
  or or_3 (XNOR_X2Y2, and_3_out, and_6_out);
  and and_7 (NOTX1_Y1, NOTX1, Y1);
  and and_8 (NOTX0_Y0, NOTX0, Y0);
  and and_9 (NOTX2_Y2, NOTX2, Y2);
  and and_10 (and_10_out, XNOR_X2Y2, NOTX1_Y1);
  and and_11 (and_11_out, XNOR_X2Y2, XNOR_X1Y1, NOTX0_Y0);
  or or_4 (N, NOTX2_Y2, and_10_out, and_11_out);
  and and_12 (E, XNOR_X0Y0, XNOR_X1Y1, XNOR_X2Y2);
endmodule

module Gray (
  input  B0,
  input  B1,
  input  B2,
  input  B3,
  output G0,
  output G1,
  output G2,
  output G3
);

  wire and_1_out, and_2_out, and_3_out, and_4_out, and_5_out, and_6_out, and_7_out, and_8_out, and_9_out,
       and_10_out, and_11_out, and_12_out, and_13_out, NOTB0, NOTB2, NOTB3, XNOR_B3B0;

  not not_1 (NOTB0, B0);
  not not_2 (G0, B1);
  not not_3 (NOTB2, B2);
  not not_4 (NOTB3, B3);
  and and_1 (and_1_out, NOTB3, NOTB0);
  and and_2 (and_2_out, B3, B0);
  or or_1 (XNOR_B3B0, and_1_out, and_2_out);
  and and_3 (and_3_out, NOTB3, G0);
  and and_4 (and_4_out, NOTB3, NOTB2, B1);
  and and_5 (and_5_out, B2, B1);
  and and_6 (and_6_out, B1, NOTB2);
  and and_7 (and_7_out, NOTB2, G0, B0);
  and and_8 (and_8_out, NOTB2, B1);
  and and_9 (and_9_out, NOTB0, G0, B2);
  and and_10 (and_10_out, and_5_out, XNOR_B3B0);
  or or_2 (G1, and_7_out, and_8_out, and_9_out);
  and and_11 (and_11_out, NOTB3, NOTB2, G0);
  and and_12 (and_12_out, and_6_out, XNOR_B3B0);
  and and_13 (and_13_out, B3, B2);
  or or_3 (G3, and_3_out, and_4_out, and_10_out);
  or or_4 (G2, and_11_out, and_12_out, and_13_out);

  // Other names for the same wires on the sheet: NOTB1 = G0
endmodule

// NOR
module FiveSeven (
  input  V,
  input  W,
  input  X,
  input  Y,
  input  Z,
  output A,
  output B,
  output C,
  output D,
  output E,
  output F,
  output G
);

  wire and_1_out, and_2_out, and_3_out, and_4_out, and_5_out, and_6_out, and_7_out, and_8_out, and_11_out,
       and_12_out, and_13_out, and_14_out, and_17_out, and_18_out, and_19_out, and_22_out, and_23_out,
       and_24_out, and_25_out, and_26_out, and_27_out, and_33_out, and_34_out, and_35_out, EIGHT, FIVE, FOUR,
       FOUR_NINE, NINE, NOTV, NOTW, NOTX, NOTY, NOTZ, ONE, ONE_SIX, or_3_out, or_4_out, or_5_out, or_8_out,
       SEVEN, SIX, THREE, THREE_EIGHT, TWO, TWO_SEVEN, XOR_WX, XOR_XY, ZERO, ZERO_FIVE;

  not not_1 (NOTV, V);
  not not_2 (NOTW, W);
  not not_3 (NOTX, X);
  not not_4 (NOTY, Y);
  not not_5 (NOTZ, Z);
  and and_1 (and_1_out, X, NOTY);
  and and_2 (and_2_out, NOTX, Y);
  and and_3 (and_3_out, NOTW, X);
  and and_4 (and_4_out, W, NOTX);
  or or_1 (XOR_XY, and_1_out, and_2_out);
  or or_2 (XOR_WX, and_3_out, and_4_out);
  and and_5 (and_5_out, V, NOTW);
  and and_6 (and_6_out, NOTV, W);
  and and_7 (and_7_out, NOTV, X);
  and and_8 (and_8_out, V, NOTX);
  or or_3 (or_3_out, V, W, X, Y);
  not not_6 (ZERO_FIVE, or_3_out);
  and and_9 (ZERO, ZERO_FIVE, NOTZ);
  and and_10 (FIVE, ZERO_FIVE, Z);
  and and_11 (and_11_out, NOTX, NOTY);
  and and_12 (and_12_out, NOTV, NOTW);
  and and_13 (and_13_out, W, NOTY);
  or or_4 (or_4_out, and_7_out, and_8_out);
  and and_14 (and_14_out, V, NOTW);
  or or_5 (or_5_out, and_5_out, and_6_out);
  and and_15 (ONE, ONE_SIX, NOTZ);
  and and_16 (SIX, ONE_SIX, Z);
  and and_17 (and_17_out, NOTV, Y);
  and and_18 (and_18_out, and_13_out, or_4_out);
  and and_19 (and_19_out, and_14_out, XOR_XY);
  and and_20 (TWO, TWO_SEVEN, NOTZ);
  and and_21 (SEVEN, TWO_SEVEN, Z);
  and and_22 (and_22_out, and_11_out, or_5_out);
  and and_23 (and_23_out, XOR_XY, and_12_out);
  or or_6 (ONE_SIX, and_22_out, and_23_out);
  and and_24 (and_24_out, XOR_WX, and_17_out);
  or or_7 (TWO_SEVEN, and_24_out, and_18_out, and_19_out);
  and and_25 (and_25_out, V, Y);
  and and_26 (and_26_out, V, NOTY);
  and and_27 (and_27_out, NOTV, Y);
  and and_28 (THREE, THREE_EIGHT, NOTZ);
  and and_29 (EIGHT, THREE_EIGHT, Z);
  and and_30 (FOUR_NINE, V, W, X, Y);
  and and_31 (FOUR, FOUR_NINE, NOTZ);
  and and_32 (NINE, FOUR_NINE, Z);
  and and_33 (and_33_out, and_25_out, XOR_WX);
  and and_34 (and_34_out, W, X);
  or or_8 (or_8_out, and_26_out, and_27_out);
  and and_35 (and_35_out, and_34_out, or_8_out);
  or or_9 (THREE_EIGHT, and_33_out, and_35_out);
  or or_10 (D, ZERO, TWO, THREE, FIVE, SIX, EIGHT);
  or or_11 (E, ZERO, TWO, SIX, EIGHT);
  or or_12 (F, ZERO, FOUR, FIVE, SIX, EIGHT, NINE);
  or or_13 (G, TWO, THREE, FOUR, FIVE, SIX, EIGHT, NINE);
  or or_14 (A, ZERO, TWO, THREE, FIVE, SIX, SEVEN, EIGHT, NINE);
  or or_15 (B, ZERO, ONE, TWO, THREE, FOUR, SEVEN, EIGHT, NINE);
  or or_16 (C, ZERO, ONE, THREE, FOUR, FIVE, SIX, SEVEN, EIGHT, NINE);
endmodule
